# Fritzing sketch 2xSN74HC595_12D (saved by Fritzing 0.9.3b)
breadboards: 1

parts:
  Part1 = Arduino Uno (Rev3)
  U1 = 74HC595 [package="DIP16 [THT]"]
  U2 = 74HC595 [package="DIP16 [THT]"]
  LED1 = smd LED [color="Red (633nm)" package="1206 [SMD]"]
  LED2 = smd LED [color="Red (633nm)" package="1206 [SMD]"]
  LED3 = smd LED [color="Red (633nm)" package="1206 [SMD]"]
  LED4 = smd LED [color="Red (633nm)" package="1206 [SMD]"]
  LED5 = smd LED [color="Red (633nm)" package="1206 [SMD]"]
  LED6 = smd LED [color="Red (633nm)" package="1206 [SMD]"]
  LED7 = smd LED [color="Red (633nm)" package="1206 [SMD]"]
  LED8 = smd LED [color="Red (633nm)" package="1206 [SMD]"]
  LED9 = smd LED [color="Red (633nm)" package="1206 [SMD]"]
  LED10 = smd LED [color="Red (633nm)" package="1206 [SMD]"]
  LED11 = smd LED [color="Red (633nm)" package="1206 [SMD]"]
  LED12 = smd LED [color="Red (633nm)" package="1206 [SMD]"]
  R2 = Resistor [tolerance=±5% resistance=330 package="0603 [SMD]"]
  R3 = Resistor [tolerance=±5% resistance=330 package="0603 [SMD]"]
  R4 = Resistor [tolerance=±5% resistance=330 package="0603 [SMD]"]
  R5 = Resistor [tolerance=±5% resistance=330 package="0603 [SMD]"]
  R6 = Resistor [tolerance=±5% resistance=330 package="0603 [SMD]"]
  R7 = Resistor [tolerance=±5% resistance=330 package="0603 [SMD]"]
  R8 = Resistor [tolerance=±5% resistance=330 package="0603 [SMD]"]
  R9 = Resistor [tolerance=±5% resistance=330 package="0603 [SMD]"]
  R10 = Resistor [tolerance=±5% resistance=330 package="0603 [SMD]"]
  R11 = Resistor [tolerance=±5% resistance=330 package="0603 [SMD]"]
  R12 = Resistor [tolerance=±5% resistance=330 package="0603 [SMD]"]
  R13 = Resistor [tolerance=±5% resistance=330 package="0603 [SMD]"]

nets:
  GND: Part1.GND, U1.GND, U1.OE, U2.GND, U2.OE, R2.Pin_0, R3.Pin_0, R4.Pin_0, R5.Pin_0, R6.Pin_0, R7.Pin_0, R8.Pin_0, R9.Pin_0, R10.Pin_0, R11.Pin_0, R12.Pin_0, R13.Pin_0
  N1: Part1.D2, U1.ST_CP, U2.ST_CP
  N2: Part1.D3_PWM, U1.SH_CP, U2.SH_CP
  N3: Part1.D4, U2.DS
  VCC: Part1.5V, U1.MR, U1.VCC, U2.MR, U2.VCC
  N4: U1.Q1, LED11.anode
  N5: U1.Q2, LED12.anode
  N6: U1.Q3, LED1.anode
  N7: U1.DS, U2.Q7'
  N8: U1.Q0, LED10.anode
  N9: U2.Q1, LED3.anode
  N10: U2.Q2, LED4.anode
  N11: U2.Q3, LED5.anode
  N12: U2.Q4, LED6.anode
  N13: U2.Q5, LED7.anode
  N14: U2.Q6, LED8.anode
  N15: U2.Q7, LED9.anode
  N16: U2.Q0, LED2.anode
  N17: LED1.cathode, R13.Pin_1
  N18: LED2.cathode, R2.Pin_1
  N19: LED3.cathode, R3.Pin_1
  N20: LED4.cathode, R4.Pin_1
  N21: LED5.cathode, R5.Pin_1
  N22: LED6.cathode, R6.Pin_1
  N23: LED7.cathode, R7.Pin_1
  N24: LED8.cathode, R8.Pin_1
  N25: LED9.cathode, R9.Pin_1
  N26: LED10.cathode, R10.Pin_1
  N27: LED11.cathode, R11.Pin_1
  N28: LED12.cathode, R12.Pin_1
