# Fritzing sketch Schematic (saved by Fritzing 0.9.3b)
breadboards: 1

parts:
  8_Channel_Relay1 = 8 Channel Power Relay
  Part1 = Arduino Uno (Rev3)
  Q1 = NPN-Transistor [package="TO92 [THT]"]
  Q2 = NPN-Transistor [package="TO92 [THT]"]
  Q3 = PNP-Transistor [package="TO92 [THT]"]
  Q4 = PNP-Transistor [package="TO92 [THT]"]
  L2 = Inductor [package="0603 [SMD]"]
  L3 = Inductor [package="0603 [SMD]"]
  L4 = Inductor [package="0603 [SMD]"]
  L5 = Inductor [package="0603 [SMD]"]
  L6 = Inductor [package="0603 [SMD]"]
  L7 = Inductor [package="0603 [SMD]"]
  L1 = Inductor [package="0603 [SMD]"]

nets:
  GND: 8_Channel_Relay1.GND, Part1.GND, Q3.C, Q4.C
  N1: 8_Channel_Relay1.IN1, Part1.D13/SCK
  N2: 8_Channel_Relay1.IN2, Part1.D12/MISO
  N3: 8_Channel_Relay1.IN3, Part1.D11_PWM/MOSI
  N4: 8_Channel_Relay1.IN4, Part1.D10_PWM/SS
  N5: 8_Channel_Relay1.IN5, Part1.D9_PWM
  N6: 8_Channel_Relay1.IN6, Part1.D8
  N7: 8_Channel_Relay1.IN7, Part1.D7
  N8: 8_Channel_Relay1.VCC#17, Part1.5V
  N9: 8_Channel_Relay1.VCC#19, 8_Channel_Relay1.JD-VCC
  N10: 8_Channel_Relay1.COM, Q1.E, Q3.E
  N11: 8_Channel_Relay1.NO#23, L6.pin_0
  N12: 8_Channel_Relay1.NO#26, L5.pin_0
  N13: 8_Channel_Relay1.NO#29, L4.pin_0
  N14: 8_Channel_Relay1.NO#32, L2.pin_0
  N15: 8_Channel_Relay1.NO#35, L7.pin_0
  N16: 8_Channel_Relay1.NO#38, L1.pin_0
  N17: 8_Channel_Relay1.NO#41, L3.pin_0
  N18: Part1.D2, Q4.B
  N19: Part1.D3_PWM, Q3.B
  N20: Part1.D4, Q2.B
  N21: Part1.D5_PWM, Q1.B
  N22: Part1.VIN, Q1.C, Q2.C
  N23: Q2.E, Q4.E, L2.pin_1, L3.pin_1, L4.pin_1, L5.pin_1, L6.pin_1, L7.pin_1, L1.pin_1

notes:
  Kalemovi predstavljaju segment od cifara (7 komada)
  NPN tranzistori
  Kolektor - 9V
  Baza - signal sa arduina 5V
  Emitor - kalemovi
  PNP tranzistori
  Kolektor - GND
  Baza - signal sa arduina 5V
  Emitor - kalemovi
  Napajanje 9V
  Napaja arduino i tranzistore
  Arduino napaja 8 relay modul i daje signale za releje (da li da budu NC-normal close ili NO -normal open)
  U zavisnosti od polozaja struja ce ili teci kroz taj odredjeni kalem ili nece uopste (kalemovi su kao sto vidis paralelno vezani)
  Ispod ovog komentara se nalazi 7 releja plus 1 sa desne strane komentara

custom parts:
  8 Channel Power Relay: An 8 channel power relay. The module operates at 5V.
