# Fritzing sketch Counter (saved by Fritzing 0.9.3b)
breadboards: 1

parts:
  Part1 = 74HC04D
  Part2 = 74HC04D
  DRIVERS1 = CD4511B
  S8 = Pushbutton [package="[SMD]"]
  S9 = Pushbutton [package="[SMD]"]
  S10 = Pushbutton [package="[SMD]"]
  S11 = Pushbutton [package="[SMD]"]
  R4 = Resistor [tolerance=±5% resistance=1k package=THT]
  R5 = Resistor [tolerance=±5% resistance=1k package=THT]
  R6 = Resistor [tolerance=±5% resistance=1k package=THT]
  R7 = Resistor [tolerance=±5% resistance=1k package=THT]
  7_Segment2 = 7 Segment Display
  Q2 = TRANSISTOR_NPN [package=to-92]
  R8 = Resistor [tolerance=±5% resistance=1k package=THT]
  Part3 = Arduino Uno (Rev3)

nets:
  GND: Part1.Y3, Part2.GND, DRIVERS1.GND1, DRIVERS1.GND, R4.Pin_1, R5.Pin_1, R6.Pin_1, R7.Pin_1, Part3.GND
  N1: Part1.Y5, 7_Segment2.Segment_B
  N2: Part1.A5, DRIVERS1.b
  N3: Part1.Y6, 7_Segment2.Segment_A
  N4: Part1.A6, DRIVERS1.a
  VCC: Part1.VCC, Part2.VCC, DRIVERS1.VCC1, DRIVERS1.VCC2, DRIVERS1.VCC, S8.Pin_3, S8.Pin_4, S9.Pin_3, S9.Pin_4, S10.Pin_3, S10.Pin_4, S11.Pin_3, S11.Pin_4, Q2.E, R8.Pin_1, Part3.5V
  N5: Part2.A1, DRIVERS1.c
  N6: Part2.Y1, 7_Segment2.Segment_C
  N7: Part2.A2, DRIVERS1.d
  N8: Part2.Y2, 7_Segment2.Segment_D
  N9: Part2.A3, DRIVERS1.e
  N10: Part2.Y3, 7_Segment2.Segment_E
  N11: Part2.Y5, 7_Segment2.Segment_G
  N12: Part2.A5, DRIVERS1.g
  N13: Part2.Y6, 7_Segment2.Segment_F
  N14: Part2.A6, DRIVERS1.f
  N15: DRIVERS1.B, S9.Pin_1, S9.Pin_2, R5.Pin_0
  N16: DRIVERS1.C, S10.Pin_1, S10.Pin_2, R6.Pin_0
  N17: DRIVERS1.D, S11.Pin_1, S11.Pin_2, R7.Pin_0
  N18: DRIVERS1.A, S8.Pin_1, S8.Pin_2, R4.Pin_0
  N19: 7_Segment2.common_anode, Q2.C
  N20: Q2.B, R8.Pin_0

custom parts:
  74HC04D: Invertor
  CD4511B: Finally....
