# Fritzing sketch Switch (saved by Fritzing 0.9.3b)
breadboards: 1

parts:
  U1 = 4017 [chip_label=4017 package="DIP (Dual Inline) [THT]"]
  U2 = 555 Timer [package="DIP8 [THT]"]
  Part1 = Arduino Uno (Rev3)
  R5 = Resistor [tolerance=±5% resistance=22k package=THT]
  U3 = POT [package=pot_alpha_rv16af-20]
  C1 = Electrolytic Capacitor [capacitance=4.7µF package="0405 [SMD, electrolytic]"]  # not connected
  LED2 = smd LED [color="Red (633nm)" package="1206 [SMD]"]
  LED3 = smd LED [color="Red (633nm)" package="1206 [SMD]"]
  LED4 = smd LED [color="Red (633nm)" package="1206 [SMD]"]
  LED5 = smd LED [color="Red (633nm)" package="1206 [SMD]"]
  LED6 = smd LED [color="Red (633nm)" package="1206 [SMD]"]
  LED7 = smd LED [color="Red (633nm)" package="1206 [SMD]"]
  LED8 = smd LED [color="Red (633nm)" package="1206 [SMD]"]
  LED9 = smd LED [color="Red (633nm)" package="1206 [SMD]"]
  LED10 = smd LED [color="Red (633nm)" package="1206 [SMD]"]
  LED11 = smd LED [color="Red (633nm)" package="1206 [SMD]"]
  R6 = Resistor [tolerance=±5% resistance=1k package=THT]

nets:
  N1: U1.pin1, LED7.anode
  N2: U1.pin2, LED3.anode
  N3: U1.pin3, LED2.anode
  N4: U1.pin4, LED4.anode
  N5: U1.pin5, LED8.anode
  N6: U1.pin6, LED9.anode
  N7: U1.pin7, LED5.anode
  N8: U1.pin8, U1.pin13, U1.pin15, U2.Ground, Part1.GND, U3.E, R6.Pin_0
  N9: U1.pin9, LED10.anode
  N10: U1.pin10, LED6.anode
  N11: U1.pin11, LED11.anode
  N12: U1.pin12, U1.pin16, U2.Reset, U2.Vcc_Supply_Voltage, Part1.5V, R5.Pin_1
  N13: U1.pin14, U2.Output
  N14: U2.Trigger, U2.Threshold, U3.S
  N15: U2.Discharge, R5.Pin_0, U3.A
  N16: LED2.cathode, R6.Pin_1

custom parts:
  4017: 4017 CMOS decade counter with 10 decoded outputs
