# Fritzing sketch SevSeg_3dig (saved by Fritzing 0.9.3b)
breadboards: 1

parts:
  Part1 = Arduino Board Ethernet
  U1 = 7-SEGMENT-DISPLAY-1_-RED [package=7-segment-1_pth]
  U2 = 7-SEGMENT-DISPLAY-1_-RED [package=7-segment-1_pth]
  U3 = 7-SEGMENT-DISPLAY-1_-RED [package=7-segment-1_pth]

nets:
  N1: Part1.D8, U1.F, U2.F, U3.F
  N2: Part1.D9_PWM, U1.G2
  N3: Part1.D0/RX, U2.G2
  N4: Part1.D1/TX, U3.G2
  N5: Part1.D2_PWM, U1.A, U2.A, U3.A
  N6: Part1.D3_PWM, U1.B, U2.B, U3.B
  N7: Part1.D4, U1.C, U2.C, U3.C
  N8: Part1.D5_PWM, U1.D, U2.D, U3.D
  N9: Part1.D6_PWM, U1.E, U2.E, U3.E
  N10: Part1.D7, U1.G, U2.G, U3.G
