# Fritzing sketch Counter (saved by Fritzing 0.9.3b)
breadboards: 1

parts:
  Part1 = 74HC04D
  Part2 = Arduino Uno (Rev3)
  Part3 = 74HC04D
  R1 = Resistor [tolerance=±5% resistance=1k package="1206 [SMD]"]
  S1 = Pushbutton [package="[THT]"]
  S2 = Pushbutton [package="[THT]"]
  S3 = Pushbutton [package="[THT]"]
  S4 = Pushbutton [package="[THT]"]
  R2 = Resistor [tolerance=±5% resistance=1k package="1206 [SMD]"]
  R3 = Resistor [tolerance=±5% resistance=1k package="1206 [SMD]"]
  R4 = Resistor [tolerance=±5% resistance=1k package="1206 [SMD]"]
  DRIVERS1 = CD4511B
  Q1 = NPN-Transistor [package="TO92 [THT]"]
  Q2 = NPN-Transistor [package="TO92 [THT]"]
  Q3 = NPN-Transistor [package="TO92 [THT]"]
  U1 = 7-SEGMENT-DISPLAY [package=7-segment-display]
  U2 = 7-SEGMENT-DISPLAY [package=7-segment-display]
  U3 = 7-SEGMENT-DISPLAY [package=7-segment-display]

nets:
  N1: Part1.A1, DRIVERS1.c
  N2: Part1.Y1, U3.DP
  N3: Part1.A2, DRIVERS1.d
  N4: Part1.Y2, U3.G1
  N5: Part1.A3, DRIVERS1.e
  N6: Part1.Y3, U3.D
  GND: Part1.GND, Part2.GND, Part3.GND, R1.Pin_0, R2.Pin_0, R3.Pin_0, R4.Pin_0, DRIVERS1.GND1, DRIVERS1.GND
  N7: Part1.Y5, U3.E
  N8: Part1.A5, DRIVERS1.g
  N9: Part1.Y6, U3.G
  N10: Part1.A6, DRIVERS1.f
  VCC: Part1.VCC, Part2.5V, Part3.VCC, S1.Pin_1, S1.Pin_2, S2.Pin_1, S2.Pin_2, S3.Pin_1, S3.Pin_2, S4.Pin_1, S4.Pin_2, DRIVERS1.VCC1, DRIVERS1.VCC2, DRIVERS1.VCC, Q1.C, Q2.C, Q3.C
  N11: Part2.D8, Q3.B
  N12: Part2.D9_PWM, DRIVERS1.A
  N13: Part2.D10_PWM/SS, DRIVERS1.B
  N14: Part2.D11_PWM/MOSI, DRIVERS1.C
  N15: Part2.D12/MISO, DRIVERS1.D
  N16: Part2.D2, R1.Pin_1, S1.Pin_3, S1.Pin_4
  N17: Part2.D3_PWM, S2.Pin_3, S2.Pin_4, R4.Pin_1
  N18: Part2.D4, S3.Pin_3, S3.Pin_4, R3.Pin_1
  N19: Part2.D5_PWM, S4.Pin_3, S4.Pin_4, R2.Pin_1
  N20: Part2.D6_PWM, Q2.B
  N21: Part2.D7, Q1.B
  N22: Part3.Y5, U3.A
  N23: Part3.A5, DRIVERS1.b
  N24: Part3.Y6, U3.G2
  N25: Part3.A6, DRIVERS1.a
  N26: Q1.E, U2.C
  N27: Q2.E, U1.C
  N28: Q3.E, U3.C

custom parts:
  74HC04D: Invertor
  CD4511B: Finally....
