# Fritzing sketch Elevator (saved by Fritzing 0.9.3b)
breadboards: 1

parts:
  Part1 = Arduino Board Ethernet
  DRIVERS1 = CD4511B
  R1 = Resistor [tolerance=±5% resistance=1k package=THT]
  LED1 = smd LED [color="Red (633nm)" package="1206 [SMD]"]
  7_Segment1 = 7 Segment Display
  S2 = Pushbutton [package="[SMD]"]
  S3 = Pushbutton [package="[SMD]"]
  S4 = Pushbutton [package="[SMD]"]
  S5 = Pushbutton [package="[SMD]"]
  S6 = Pushbutton [package="[SMD]"]
  LED2 = smd LED [color="Red (633nm)" package="1206 [SMD]"]
  LED3 = smd LED [color="Red (633nm)" package="1206 [SMD]"]
  LED4 = smd LED [color="Red (633nm)" package="1206 [SMD]"]
  LED5 = smd LED [color="Red (633nm)" package="1206 [SMD]"]
  R3 = Resistor [tolerance=±5% resistance=1k package=THT]
  R4 = Resistor [tolerance=±5% resistance=1k package=THT]
  R5 = Resistor [tolerance=±5% resistance=1k package=THT]
  R6 = Resistor [tolerance=±5% resistance=1k package=THT]
  R8 = Resistor [tolerance=±5% resistance=220 package=THT]
  R9 = Resistor [tolerance=±5% resistance=220 package=THT]
  R10 = Resistor [tolerance=±5% resistance=220 package=THT]
  R11 = Resistor [tolerance=±5% resistance=220 package=THT]
  R12 = Resistor [tolerance=±5% resistance=220 package=THT]
  Part2 = 74HC04D
  Part3 = 74HC04D
  Q1 = TRANSISTOR_NPN [package=to-92]
  R13 = Resistor [tolerance=±5% resistance=1k package=THT]
  R14 = Resistor [tolerance=±5% resistance=1k package=THT]
  S7 = Pushbutton [package="[SMD]"]

nets:
  N1: Part1.D8, S3.Pin_3, S3.Pin_4, R4.Pin_1
  N2: Part1.D9_PWM, S4.Pin_3, S4.Pin_4, R5.Pin_1
  VCC: Part1.D11/MOSI, Part1.5V, DRIVERS1.VCC1, DRIVERS1.VCC2, DRIVERS1.VCC, S2.Pin_1, S2.Pin_2, S3.Pin_1, S3.Pin_2, S4.Pin_1, S4.Pin_2, S5.Pin_1, S5.Pin_2, S6.Pin_1, S6.Pin_2, Part2.VCC, Part3.VCC, Q1.E, S7.Pin_1, S7.Pin_2
  N3: Part1.A0, R14.Pin_0
  N4: Part1.A1, LED2.anode
  N5: Part1.A2, LED3.anode
  N6: Part1.A3, LED4.anode
  N7: Part1.A4, LED5.anode
  N8: Part1.D2_PWM, DRIVERS1.A
  N9: Part1.D3_PWM, DRIVERS1.B
  N10: Part1.D4, DRIVERS1.C
  N11: Part1.D5_PWM, DRIVERS1.D
  N12: Part1.D6_PWM, R13.Pin_1, S7.Pin_3, S7.Pin_4
  N13: Part1.D7, S2.Pin_3, S2.Pin_4, R3.Pin_1
  GND: Part1.GND, DRIVERS1.GND1, DRIVERS1.GND, R1.Pin_0, R3.Pin_0, R4.Pin_0, R5.Pin_0, R6.Pin_0, R8.Pin_0, R9.Pin_0, R10.Pin_0, R11.Pin_0, R12.Pin_0, Part2.GND, Part3.GND, R13.Pin_0
  N14: DRIVERS1.e, Part3.A3
  N15: DRIVERS1.d, Part3.A2
  N16: DRIVERS1.c, Part3.A1
  N17: DRIVERS1.b, Part2.A5
  N18: DRIVERS1.a, Part2.A6
  N19: DRIVERS1.g, Part3.A5
  N20: DRIVERS1.f, Part3.A6
  N21: R1.Pin_1, S6.Pin_3, S6.Pin_4
  N22: LED1.cathode, R12.Pin_1
  N23: 7_Segment1.Segment_E, Part3.Y3
  N24: 7_Segment1.Segment_D, Part3.Y2
  N25: 7_Segment1.common_anode, Q1.C
  N26: 7_Segment1.Segment_C, Part3.Y1
  N27: 7_Segment1.Segment_B, Part2.Y5
  N28: 7_Segment1.Segment_A, Part2.Y6
  N29: 7_Segment1.Segment_F, Part3.Y6
  N30: 7_Segment1.Segment_G, Part3.Y5
  N31: S5.Pin_3, S5.Pin_4, R6.Pin_1
  N32: LED2.cathode, R11.Pin_1
  N33: LED3.cathode, R8.Pin_1
  N34: LED4.cathode, R9.Pin_1
  N35: LED5.cathode, R10.Pin_1
  N36: Q1.B, R14.Pin_1

custom parts:
  CD4511B: Finally....
  74HC04D: Invertor
