# Fritzing sketch I2C_SPI (saved by Fritzing 0.9.3b)
breadboards: 1

parts:
  Part1 = Arduino Uno (Rev3)
  LCM1602_I2C1 = LCM1602 I2C [part_number="LCM1602 IIC" chip_label="LCM1602 IIC" package="DIP (Dual Inline) [THT]"]
  LCD1 = LCD screen
  Part2 = prefix101218 [part_number=101218]
  ZS-042_RTC1 = ZS-042 RTC Module
  8x8_LED_Modul_mit_MAX1 = 8x8 LED Modul mit MAX7219 [package=THT]
  8x8_LED_Modul_mit_MAX2 = 8x8 LED Modul mit MAX7219 [package=THT]
  8x8_LED_Modul_mit_MAX3 = 8x8 LED Modul mit MAX7219 [package=THT]
  8x8_LED_Modul_mit_MAX4 = 8x8 LED Modul mit MAX7219 [package=THT]
  Part3 = Adafruit BMP180
  LED1 = LED - 3mm [color="Red (633nm)" package="3 mm [THT]"]
  LED2 = LED - 3mm [color="Red (633nm)" package="3 mm [THT]"]
  R1 = Resistor [tolerance=±5% resistance=220 package=THT]
  R2 = Resistor [tolerance=±5% resistance=220 package=THT]
  U1 = Voltage Regulator - 5V [package="DPak [SMD]"]
  C1 = Electrolytic Capacitor [capacitance=1µF package="100 mil [THT, electrolytic]"]

nets:
  N1: Part1.A4/SDA, LCM1602_I2C1.SDA, ZS-042_RTC1.SDA, Part3.SDA
  N2: Part1.A5/SCL, LCM1602_I2C1.SCL, ZS-042_RTC1.SCL, Part3.SCL
  N3: Part1.D8, Part2.connector8
  N4: Part1.D9_PWM, 8x8_LED_Modul_mit_MAX1.CS_Eingang
  N5: Part1.D11_PWM/MOSI, Part2.connector10, 8x8_LED_Modul_mit_MAX1.DIN_Eingang
  N6: Part1.D12/MISO, Part2.connector11
  N7: Part1.D13/SCK, Part2.connector9, 8x8_LED_Modul_mit_MAX1.CLK_Eingang
  N8: Part1.D4, LED1.anode
  N9: Part1.D5_PWM, LED2.anode
  N10: Part1.D7, Part2.connector14
  3V3: Part1.3V3, Part2.connector15, ZS-042_RTC1.VCC, Part3.+3V3
  5V: Part1.5V, LCM1602_I2C1.VCC
  GND: Part1.GND, LCM1602_I2C1.GND, Part2.connector13, ZS-042_RTC1.GND, 8x8_LED_Modul_mit_MAX1.GND_Eingang, Part3.GND, R1.Pin_1, R2.Pin_1, U1.GND, C1.-
  N11: Part1.VIN, U1.input_voltage
  VSS: LCM1602_I2C1.VSS, LCD1.VSS
  VDD: LCM1602_I2C1.VDD, LCD1.VDD
  N12: LCM1602_I2C1.V0, LCD1.V0
  N13: LCM1602_I2C1.RS, LCD1.RS
  N14: LCM1602_I2C1.RW, LCD1.R/W
  N15: LCM1602_I2C1.E, LCD1.E
  N16: LCM1602_I2C1.D0, LCD1.DB0
  N17: LCM1602_I2C1.D1, LCD1.DB1
  N18: LCM1602_I2C1.D2, LCD1.DB2
  N19: LCM1602_I2C1.D3, LCD1.DB3
  N20: LCM1602_I2C1.D4, LCD1.DB4
  N21: LCM1602_I2C1.D5, LCD1.DB5
  N22: LCM1602_I2C1.D6, LCD1.DB6
  N23: LCM1602_I2C1.D7, LCD1.DB7
  N24: LCM1602_I2C1.A, LCD1.LED+
  N25: LCM1602_I2C1.K, LCD1.LED-
  N26: LCM1602_I2C1.LED_A, LCM1602_I2C1.LED_B
  N27: 8x8_LED_Modul_mit_MAX1.VCC_Eingang, U1.output_voltage, C1.+
  N28: 8x8_LED_Modul_mit_MAX1.VCC_Ausgang, 8x8_LED_Modul_mit_MAX2.VCC_Eingang
  N29: 8x8_LED_Modul_mit_MAX1.GND_Ausgang, 8x8_LED_Modul_mit_MAX2.GND_Eingang
  N30: 8x8_LED_Modul_mit_MAX1.DOUT_Ausgang, 8x8_LED_Modul_mit_MAX2.DIN_Eingang
  N31: 8x8_LED_Modul_mit_MAX1.CS_Ausgang, 8x8_LED_Modul_mit_MAX2.CS_Eingang
  N32: 8x8_LED_Modul_mit_MAX1.CLK_Ausgang, 8x8_LED_Modul_mit_MAX2.CLK_Eingang
  N33: 8x8_LED_Modul_mit_MAX2.VCC_Ausgang, 8x8_LED_Modul_mit_MAX3.VCC_Eingang
  N34: 8x8_LED_Modul_mit_MAX2.GND_Ausgang, 8x8_LED_Modul_mit_MAX3.GND_Eingang
  N35: 8x8_LED_Modul_mit_MAX2.DOUT_Ausgang, 8x8_LED_Modul_mit_MAX3.DIN_Eingang
  N36: 8x8_LED_Modul_mit_MAX2.CS_Ausgang, 8x8_LED_Modul_mit_MAX3.CS_Eingang
  N37: 8x8_LED_Modul_mit_MAX2.CLK_Ausgang, 8x8_LED_Modul_mit_MAX3.CLK_Eingang
  N38: 8x8_LED_Modul_mit_MAX3.VCC_Ausgang, 8x8_LED_Modul_mit_MAX4.VCC_Eingang
  N39: 8x8_LED_Modul_mit_MAX3.GND_Ausgang, 8x8_LED_Modul_mit_MAX4.GND_Eingang
  N40: 8x8_LED_Modul_mit_MAX3.DOUT_Ausgang, 8x8_LED_Modul_mit_MAX4.DIN_Eingang
  N41: 8x8_LED_Modul_mit_MAX3.CS_Ausgang, 8x8_LED_Modul_mit_MAX4.CS_Eingang
  N42: 8x8_LED_Modul_mit_MAX3.CLK_Ausgang, 8x8_LED_Modul_mit_MAX4.CLK_Eingang
  N43: LED1.cathode, R2.Pin_0
  N44: LED2.cathode, R1.Pin_0

notes:
  GND
  +7 - +12V DC
  7805 regulator

custom parts:
  LCM1602 I2C: I2C-Module to use a 1602 or 2004 LCD on with the wire.h libory Serial LCD Modul
  Adafruit BMP180: This precision sensor from Bosch is the best low-cost sensing solution for measuring barometric pressure and temperature. Because pressure changes with altitude you can also use it as an altimeter! The sensor is soldered onto a PCB with a 3.3V regulator, I2C level shifter and pull-up resistors on the I2C pins. The BMP180 is the next-generation of sensors from Bosch, and replaces the BMP085.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
