# Fritzing sketch Schematic (saved by Fritzing 0.9.3b)

parts:
  Part1 = Arduino Uno (Rev3)
  Part2 = Arduino Uno (Rev3)
  Part3 = Arduino Uno (Rev3)
  R1 = Resistor [tolerance=±5% resistance=220 package=THT]
  R2 = Resistor [tolerance=±5% resistance=220 package=THT]
  R3 = Resistor [tolerance=±5% resistance=220 package=THT]
  LED1 = LED - 5mm [color="Red (633nm)" package="5 mm [THT]"]
  LED2 = LED - 5mm [color="Red (633nm)" package="5 mm [THT]"]
  LED3 = LED - 5mm [color="Red (633nm)" package="5 mm [THT]"]

nets:
  N1: Part1.D8, R3.Pin_0
  N2: Part1.GND, LED2.cathode
  N3: Part1.D0/RX, Part3.D1/TX
  N4: Part1.D1/TX, Part2.D0/RX
  N5: Part2.D8, R2.Pin_0
  N6: Part2.GND, LED3.cathode
  N7: Part2.D1/TX, Part3.D0/RX
  N8: Part3.D8, R1.Pin_0
  N9: Part3.GND, LED1.cathode
  N10: R1.Pin_1, LED1.anode
  N11: R2.Pin_1, LED3.anode
  N12: R3.Pin_1, LED2.anode
