# Fritzing sketch Schematic (saved by Fritzing 0.9.3b)
breadboards: 1

parts:
  U1 = RS485 [package=so08]
  U2 = RS485 [package=so08]
  Part1 = Arduino Uno (Rev3)
  Part2 = Arduino Uno (Rev3)

nets:
  N1: U1.RO, Part1.D0/RX
  N2: U1._RE, U1.DE, Part1.D8
  N3: U1.DI, Part1.D1/TX
  GND: U1.GND, U2.GND, Part1.GND, Part2.GND
  N4: U1.A, U2.A
  N5: U1.B, U2.B
  VCC: U1.VCC, U2.VCC, Part1.5V, Part2.5V
  N6: U2.RO, Part2.D0/RX
  N7: U2._RE, U2.DE, Part2.D8
  N8: U2.DI, Part2.D1/TX
