# Fritzing sketch SchematicTaster (saved by Fritzing 0.9.3b)
breadboards: 1

parts:
  U1 = RS485 [package=so08]
  U2 = RS485 [package=so08]
  R1 = Resistor [tolerance=±5% resistance=220 package="0805 [SMD]"]
  R2 = Resistor [tolerance=±5% resistance=220 package="0805 [SMD]"]
  R3 = Resistor [tolerance=±5% resistance=220 package="0805 [SMD]"]
  LED1 = smd LED [color="Red (633nm)" package="0805 [SMD]"]
  LED2 = smd LED [color="Red (633nm)" package="0805 [SMD]"]
  Part1 = Arduino Uno (Rev3)
  Part2 = Arduino Uno (Rev3)
  S1 = Pushbutton [package="[THT]"]

nets:
  N1: U1.RO, Part2.D0/RX
  N2: U1._RE, U1.DE
  N3: U1.DI, Part2.D1/TX
  GND: U1.GND, LED2.cathode, Part2.GND
  N4: U1.A, U2.A
  N5: U1.B, U2.B
  VCC: U1.VCC, Part2.5V
  N6: U2.RO, Part1.D0/RX
  N7: U2._RE, U2.DE, Part1.D8
  N8: U2.DI, Part1.D1/TX
  N9: U2.GND, R2.Pin_0, LED1.cathode
  VCC_2: U2.VCC, Part1.5V, S1.Pin_1, S1.Pin_2
  N10: R1.Pin_0, LED2.anode
  N11: R1.Pin_1, Part2.D9_PWM
  N12: R2.Pin_1, Part1.D10_PWM/SS, S1.Pin_3, S1.Pin_4
  N13: R3.Pin_0, LED1.anode
  N14: R3.Pin_1, Part1.D9_PWM
