# Fritzing sketch SN74HC595N (saved by Fritzing 0.9.3b)
breadboards: 1

parts:
  Part1 = Arduino Board Ethernet
  U2 = 74HC595 [package="DIP16 [THT]"]
  S1 = Pushbutton [package="[THT]"]
  S2 = Pushbutton [package="[THT]"]
  R1 = Resistor [tolerance=±5% resistance=1k package="2010 [SMD]"]
  R2 = Resistor [tolerance=±5% resistance=1k package="2010 [SMD]"]
  U4 = 7-SEGMENT-DISPLAY [package=7-segment-display]
  R3 = Resistor [tolerance=±5% resistance=660 package="2010 [SMD]"]
  U5 = 7-SEGMENT-DISPLAY [package=7-segment-display]
  U6 = 7-SEGMENT-DISPLAY [package=7-segment-display]
  R4 = Resistor [tolerance=±5% resistance=660 package="2010 [SMD]"]
  R5 = Resistor [tolerance=±5% resistance=660 package="2010 [SMD]"]

nets:
  N1: Part1.D8, R5.Pin_1
  N2: Part1.D9_PWM, R4.Pin_1
  N3: Part1.D2_PWM, S2.Pin_3, S2.Pin_4, R1.Pin_1
  N4: Part1.D3_PWM, S1.Pin_3, S1.Pin_4, R2.Pin_1
  N5: Part1.D4, U2.SH_CP
  N6: Part1.D5_PWM, U2.DS
  N7: Part1.D6_PWM, U2.ST_CP
  N8: Part1.D7, R3.Pin_1
  5V: Part1.5V, U2.VCC, S1.Pin_1, S1.Pin_2, S2.Pin_1, S2.Pin_2
  GND: Part1.GND, U2.GND, U2.MR, U2.OE, R1.Pin_0, R2.Pin_0
  N9: U2.Q1, U4.G2
  N10: U2.Q2, U4.A
  N11: U2.Q3, U6.DP
  N12: U2.Q4, U6.G1
  N13: U2.Q5, U6.D
  N14: U2.Q6, U4.E
  N15: U2.Q7, U4.G
  N16: U4.F, R3.Pin_0
  N17: U5.F, R5.Pin_0
  N18: U6.F, R4.Pin_0
