# Fritzing sketch Schematic (saved by Fritzing 0.9.3b)
breadboards: 1

parts:
  Part1 = Arduino Nano (Rev3.0)
  Part2 = Arduino Nano (Rev3.0)
  Part3 = Arduino Uno (Rev3)
  LED1 = LED - 5mm [color="Red (633nm)" package="5 mm [THT]"]
  LED2 = LED - 5mm [color="Red (633nm)" package="5 mm [THT]"]
  R1 = Resistor [tolerance=±5% resistance=1k package="2512 [SMD]"]
  R2 = Resistor [tolerance=±5% resistance=1k package="2512 [SMD]"]
  R3 = Resistor [tolerance=±5% resistance=220 package="2512 [SMD]"]
  R4 = Resistor [tolerance=±5% resistance=220 package="2512 [SMD]"]
  S1 = Pushbutton [package="[SMD]"]
  S2 = Pushbutton [package="[SMD]"]

nets:
  N1: Part1.GND, LED2.cathode
  N2: Part1.D7, R3.Pin_1
  N3: Part1.D10, Part3.D8
  N4: Part1.D11/MOSI, Part2.D11/MOSI, Part3.D11_PWM/MOSI
  N5: Part1.D12/MISO, Part2.D12/MISO, Part3.D12/MISO
  N6: Part1.D13/SCK, Part2.D13/SCK, Part3.D13/SCK
  N7: Part2.GND, R4.Pin_1
  N8: Part2.D7, LED1.anode
  N9: Part2.D10, Part3.D9_PWM
  N10: Part3.D6_PWM, R1.Pin_0, S2.Pin_1, S2.Pin_2
  N11: Part3.D7, R2.Pin_1, S1.Pin_1, S1.Pin_2
  N12: Part3.5V, S1.Pin_3, S1.Pin_4, S2.Pin_3, S2.Pin_4
  N13: Part3.GND, R1.Pin_1, R2.Pin_0
  N14: LED1.cathode, R4.Pin_0
  N15: LED2.anode, R3.Pin_0
