# Fritzing sketch SevSeg_3dig (saved by Fritzing 0.9.3b)
breadboards: 1

parts:
  Part1 = Arduino Board Ethernet
  R1 = Resistor [tolerance=±5% resistance=660 package="2010 [SMD]"]
  7_Segment1 = 7 Segment Display
  7_Segment2 = 7 Segment Display
  R2 = Resistor [tolerance=±5% resistance=660 package="2010 [SMD]"]
  7_Segment3 = 7 Segment Display
  R3 = Resistor [tolerance=±5% resistance=660 package="2010 [SMD]"]

nets:
  N1: Part1.D8, 7_Segment3.Segment_F
  N2: Part1.D9_PWM, R1.Pin_1
  N3: Part1.D10_PWM/SS, R2.Pin_1
  N4: Part1.D11/MOSI, R3.Pin_1
  N5: Part1.D2_PWM, 7_Segment3.Segment_A
  N6: Part1.D3_PWM, 7_Segment3.Segment_B
  N7: Part1.D4, 7_Segment3.Segment_C
  N8: Part1.D5_PWM, 7_Segment3.Segment_D
  N9: Part1.D6_PWM, 7_Segment3.Segment_E
  N10: Part1.D7, 7_Segment3.Segment_G
  N11: R1.Pin_0, 7_Segment1.common_anode
  N12: 7_Segment2.common_anode, R2.Pin_0
  N13: 7_Segment3.common_anode, R3.Pin_0
